// Logisim project Project2_Skeleton.circ as structural Verilog: 7 circuits, main circuit Multi_Purpose_Processor
module Incrementor (
  input  [3:0] A,
  output [3:0] Q
);

  Adder #(.width(4)) adder_1 (.a(A), .b(4'b0001), .out(Q));  // open: cin, cout
endmodule

module Arithmetic_Logic_Unit (
  input  [3:0] A,
  input  [3:0] B,
  input  [2:0] Opcode,
  output [3:0] Q,
  output Z_flag
);

  wire [0:0] comparator_1_eq;
  wire [3:0] adder_1_out, incrementor_1_q, multiplier_1_out, not_1_out, subtractor_1_out, xor_1_out;

  assign not_1_out = ~A;  // NOT_Gate not_1, 4 bits wide
  Comparator #(.width(4)) comparator_1 (.a(A), .b(B), .eq(comparator_1_eq[0]));  // open: gt, lt
  assign xor_1_out = A ^ B;  // XOR_Gate xor_1, 4 bits wide
  Adder #(.width(4)) adder_1 (.a(A), .b(B), .out(adder_1_out));  // open: cin, cout
  Subtractor #(.width(4)) subtractor_1 (.a(A), .b(B), .out(subtractor_1_out));  // open: bin, bout
  Multiplier #(.width(4)) multiplier_1 (.a(A), .b(B), .out(multiplier_1_out));  // open: cin, cout
  Incrementor incrementor_1 (.A(A), .Q(incrementor_1_q));
  Multiplexer #(.select(3), .width(4)) multiplexer_1 (
    .in0(B), .in1({3'b000, comparator_1_eq[0]}), .in2(xor_1_out), .in3(not_1_out), .in4(incrementor_1_q),
    .in5(adder_1_out), .in6(subtractor_1_out), .in7(multiplier_1_out), .out(Q), .sel(Opcode));
  nor nor_1 (Z_flag, Q[0], Q[1], Q[2], Q[3]);
endmodule

module Register_File (
  input  [3:0] D,
  input  WE,
  input  [1:0] W_id,
  input  [1:0] R_id_A,
  input  [1:0] R_id_B,
  input  Clk,
  input  Reset,
  output [3:0] Q_A,
  output [3:0] Q_B
);

  wire decoder_1_out0, decoder_1_out1, decoder_1_out2, decoder_1_out3;
  wire [3:0] R_00_q, R_01_q, R_10_q, R_11_q;

  Decoder #(.select(2)) decoder_1 (
    .out0(decoder_1_out0), .out1(decoder_1_out1), .out2(decoder_1_out2), .out3(decoder_1_out3), .sel(W_id),
    .en(WE));
  Register #(.width(4)) R_00 (.D(D), .en(decoder_1_out0), .clk(Clk), .Q(R_00_q), .clr(Reset));
  Register #(.width(4)) R_01 (.D(D), .en(decoder_1_out1), .clk(Clk), .Q(R_01_q), .clr(Reset));
  Register #(.width(4)) R_10 (.D(D), .en(decoder_1_out2), .clk(Clk), .Q(R_10_q), .clr(Reset));
  Register #(.width(4)) R_11 (.D(D), .en(decoder_1_out3), .clk(Clk), .Q(R_11_q), .clr(Reset));
  Multiplexer #(.select(2), .width(4)) multiplexer_1 (
    .in0(R_00_q), .in1(R_01_q), .in2(R_10_q), .in3(R_11_q), .out(Q_A), .sel(R_id_A));
  Multiplexer #(.select(2), .width(4)) multiplexer_2 (
    .in0(R_00_q), .in1(R_01_q), .in2(R_10_q), .in3(R_11_q), .out(Q_B), .sel(R_id_B));
endmodule

module Flag_Register (
  input  Z_in,
  input  WE,
  input  Clk,
  input  Reset,
  output Z_flag
);

  wire d_ff_1_qn, multiplexer_1_out;

  D_Flip_Flop d_ff_1 (.D(multiplexer_1_out), .clk(Clk), .Q(Z_flag), .Qn(d_ff_1_qn), .reset(Reset));  // open: preset
  Multiplexer multiplexer_1 (.in0(Z_flag), .in1(Z_in), .out(multiplexer_1_out), .sel(WE));
  // NoConnect on d_ff_1_qn
endmodule

module PC_Register (
  input  [3:0] Jump_Addr,
  input  Do_Jump,
  input  Clk,
  input  Reset,
  output [3:0] M_addr
);

  Multiplexer #(.width(4)) multiplexer_1 ();  // open: in0, in1, out, sel
  Incrementor incrementor_1 ();  // open: A, Q
  Register #(.width(4)) register_1 (.en(1'b1));  // open: D, clk, Q, clr
endmodule

module Control_Unit (
  input  [8:0] M,
  input  Z_flag,
  output WE,
  output [1:0] W_id,
  output [1:0] R_id_A,
  output [1:0] R_id_B,
  output [2:0] Opcode,
  output Operand,
  output Do_Jump,
  output [3:0] Jump_Addr
);
endmodule

module Multi_Purpose_Processor (
  input  [3:0] I,
  input  Reset,
  output [3:0] Q_A,
  output [3:0] Q_B
);

  Clock clock_1 ();  // open: out
  ROM #(.addrWidth(4), .dataWidth(9)) rom_1 ();  // open: addr, data
  Multiplexer #(.width(4)) multiplexer_1 ();  // open: in0, in1, out, sel
endmodule
